# Fritzing sketch gps_circuito (saved by Fritzing 0.9.3b)
circuit board: 8.46667cm x 5.64444cm
breadboards: 1

parts:
  LED1 = LED - 5mm [color="Red (633nm)" package="5 mm [THT]"]
  R1 = Resistor [tolerance=±5% resistance=220 package=THT]
  U2 = Voltage Regulator - 5V [package="TO220 [THT]"]
  U3 = GP-2106 [package=gp-2106]
  JP2 = Header 4 [package=molex-1x4_lock]
  JP1 = Header 6 [package=1x06-smd]

nets:
  GND: LED1.cathode, U2.GND, U3.GND, JP2.4, JP1.4
  N1: LED1.anode, R1.Pin_1
  N2: R1.Pin_0, U2.output_voltage, U3.VCC, JP2.1
  N3: U2.input_voltage, JP1.5
  N4: U3.RX, JP2.2, JP1.2
  N5: U3.TX, JP2.3, JP1.3
