# Fritzing sketch bruce (saved by Fritzing 0.9.0b)

parts:
  Componente1 = Arduino Mega 2560 (Rev3)
  Componente2 = 9 Degrees of Freedom - Sensor Stick
  U2 = GP-2106 [package=gp-2106]
  MD03A1 = Dual VNH2SP30 Motor Driver [part_number=MD03A]
  MD03A2 = Dual VNH2SP30 Motor Driver [part_number=MD03A]
  MD03A3 = Dual VNH2SP30 Motor Driver [part_number=MD03A]
  U8 = HC-SR04 [chip_label=IC package="SIP (Single Inline) [THT]"]
  LED1 = LEDs [package=led10mm]
  Q1 = TRANSISTOR_NPN [package=to-92-ammo]
  U9 = Voltage Regulator - 5V [package="DPak [SMD]"]
  U10 = Voltage Regulator - 5V [package="DPak [SMD]"]
  U11 = Voltage Regulator - 5V [package="DPak [SMD]"]
  U12 = Voltage Regulator - 5V [package="DPak [SMD]"]
  R2 = Photocell (LDR) [package=THT]
  U14 = Voltage Regulator - 5V [package="DPak [SMD]"]
  U17 = RF-LINK_RX [package=rf-link_rx]
  U15 = Voltage Regulator - 5V [package="DPak [SMD]"]
  R5 = Resistor [tolerance=±5% resistance=10k package=THT]
  R6 = Resistor [tolerance=±5% resistance=27k package=THT]
  LED2 = LEDs [package=led10mm]
  R7 = Resistor [tolerance=±5% resistance=100 package=THT]
  M1 = DC Motor
  M2 = DC Motor
  S1 = Round Pushbutton
  S2 = Round Pushbutton
  R8 = Resistor [tolerance=±5% resistance=100 package=THT]

nets:
  N1: Componente1.A0, R2.pin_1, R6.Pin_0
  N2: Componente1.D21/SCL, Componente2.SCL
  N3: Componente1.D20/SDA, Componente2.SDA
  N4: Componente1.D19/RX1, U2.TX
  N5: Componente1.D18/TX1, U2.RX
  GND: Componente1.GND, MD03A1.GND, MD03A2.GND, MD03A3.GND, S1.leg1, S2.leg1
  N6: Componente1.RESET, S1.leg0
  N7: Componente1.5V, R8.Pin_1
  N8: Componente1.D2_PWM, MD03A1.PWM, MD03A2.PWM, MD03A3.PWM
  N9: Componente1.D3_PWM, MD03A1.2PWM, MD03A2.2PWM, MD03A3.2PWM
  N10: Componente1.D4_PWM, MD03A1.1INa, MD03A2.1INa, MD03A3.1INa
  N11: Componente1.D5_PWM, MD03A1.1INb, MD03A2.1INb, MD03A3.1INb
  N12: Componente1.D6_PWM, MD03A1.2INb#142, MD03A2.2INb#142, MD03A3.2INb#142
  N13: Componente1.D7_PWM, MD03A1.2INb#143, MD03A2.2INb#143, MD03A3.2INb#143
  N14: Componente1.D31, U8.Trig
  N15: Componente1.D33, U8.Echo
  N16: Componente1.D46, U17.Data#2
  N17: Componente1.D50, S2.leg0, R8.Pin_0
  N18: Componente1.D52, R5.Pin_0
  GND_2: Componente2.GND, U11.GND
  N19: Componente2.VCC, U11.output_voltage
  GND_3: U2.GND, U10.GND
  N20: U2.VCC, U10.output_voltage
  N21: MD03A1.OUT_1A, M1.pin_1
  N22: MD03A1.OUT_1B, M1.pin_2
  N23: MD03A1.OUT_2A, M2.pin_1
  N24: MD03A1.OUT_2B, M2.pin_2
  N25: U8.Vcc, U14.output_voltage
  GND_4: U8.GND, U14.GND
  N26: LED1.A, Q1.E
  N27: LED1.C, U9.output_voltage
  N28: Q1.B, R5.Pin_1
  N29: Q1.C, U9.GND
  N30: U12.GND, R2.pin_0, LED2.A
  N31: U12.output_voltage, R6.Pin_1, R7.Pin_1
  GND_5: U17.GND, U15.input_voltage, U15.GND
  N32: U17.Data#3, U17.VCC, U15.output_voltage
  N33: LED2.C, R7.Pin_0

custom parts:
  HC-SR04: HC-SR04 ultrasound distance sensor
  RF-LINK_RX: RF Link receivers- WRL-8947, 8948, 8949, 8950
